# Fritzing sketch simple_pedestrian_crossing (saved by Fritzing 0.9.3b)
circuit board: 8.46667cm x 5.64444cm
breadboards: 1

parts:
  Traffic_Light = Arduino Uno (Rev3)
  LED1 = LED - 5mm [color="Red (633nm)" package="5 mm [THT]"]
  LED2 = LED - 5mm [color="Yellow (595nm)" package="5 mm [THT]"]
  LED3 = LED - 5mm [color="Green (555nm)" package="5 mm [THT]"]
  S1 = Pushbutton [package="[THT]"]
  R6 = Resistor [tolerance=±1% resistance=10k package=THT]
  R5 = Resistor [tolerance=±1% resistance=220 package=THT]
  R4 = Resistor [tolerance=±1% resistance=220 package=THT]
  R3 = Resistor [tolerance=±1% resistance=220 package=THT]

nets:
  N1: Traffic_Light.D8, LED3.anode
  N2: Traffic_Light.D9_PWM, LED2.anode
  N3: Traffic_Light.D10_PWM/SS, LED1.anode
  N4: Traffic_Light.GND, R6.Pin_0, R5.Pin_0, R4.Pin_0, R3.Pin_0
  N5: Traffic_Light.D2, S1.Pin_3, S1.Pin_4, R6.Pin_1
  N6: Traffic_Light.5V, S1.Pin_1, S1.Pin_2
  N7: LED1.cathode, R3.Pin_1
  N8: LED2.cathode, R4.Pin_1
  N9: LED3.cathode, R5.Pin_1
